// Logisim project seq_circuit.circ as structural Verilog: 1 circuit, main circuit main
module main (
  input  x,
  input  y,
  input  Q,
  input  C,
  output S,
  output C_2,
  output Q_2
);

  wire and_1_out, and_2_out, clock_1_out, undriven, xor_1_out, xor_3_out;

  xor xor_1 (xor_1_out, x, y);
  and and_1 (and_1_out, x, y);
  xor xor_2 (S, xor_1_out, Q);
  and and_2 (and_2_out, xor_1_out, Q);
  xor xor_3 (xor_3_out, Q_2, C);
  or or_1 (C_2, and_2_out, and_1_out);
  Clock clock_1 (.out(clock_1_out));
  D_Flip_Flop #(.Pre_Clr_Positions("LEGACY"), .enable("true")) d_ff_1 (
    .clk(clock_1_out), .D(xor_3_out), .Q(Q_2), .reset(undriven));  // open: Qn, preset, en
endmodule
